# Fritzing sketch Arbeitsprobe (saved by Fritzing 0.9.3b)
breadboards: 1

parts:
  LCD1 = LCD screen
  R1 = Resistor [tolerance=±5% resistance=220 package=THT]
  Part1 = Arduino Uno (Rev3)
  R2 = Trimmer Potentiometer [maximum_resistance=10kΩ package=THT]
  LED1 = LED - 5mm [color="Red (633nm)" package="5 mm [THT]"]
  LED2 = LED - 5mm [color="Yellow (595nm)" package="5 mm [THT]"]
  LED3 = LED - 5mm [color="Green (560nm)" package="5 mm [THT]"]
  R3 = Resistor [tolerance=±5% resistance=220 package=THT]
  R4 = Resistor [tolerance=±5% resistance=220 package=THT]
  R5 = Resistor [tolerance=±5% resistance=220 package=THT]
  T1 = LM35 Temperature Sensor [package="TO92 [THT]"]
  S1 = Pushbutton [package="[THT]"]
  LED4 = LED - 5mm [color="Blue (525nm)" package="5 mm [THT]"]
  R6 = Resistor [tolerance=±5% resistance=220 package=THT]
  R7 = Resistor [tolerance=±5% resistance=10k package=THT]

nets:
  GND: LCD1.VSS, LCD1.R/W, LCD1.LED-, Part1.GND, R2.leg1, R3.Pin_0, R4.Pin_0, R5.Pin_0, T1.GND, R6.Pin_0, R7.Pin_0
  VDD: LCD1.VDD, R1.Pin_1, Part1.5V, R2.leg2, T1.+Vs
  N1: LCD1.V0, R2.wiper
  N2: LCD1.RS, Part1.D13/SCK
  N3: LCD1.E, Part1.D12/MISO
  N4: LCD1.DB4, Part1.D11_PWM/MOSI
  N5: LCD1.DB5, Part1.D10_PWM/SS
  N6: LCD1.DB6, Part1.D9_PWM
  N7: LCD1.DB7, Part1.D8
  N8: LCD1.LED+, R1.Pin_0
  N9: Part1.A0, T1.Vout
  N10: Part1.D2, LED1.anode
  N11: Part1.D3_PWM, LED2.anode
  N12: Part1.D4, LED3.anode
  N13: Part1.D5_PWM, S1.Pin_1, S1.Pin_2, R7.Pin_1
  N14: Part1.D6_PWM, LED4.anode
  N15: LED1.cathode, R5.Pin_1
  N16: LED2.cathode, R4.Pin_1
  N17: LED3.cathode, R3.Pin_1
  N18: LED4.cathode, R6.Pin_1

// code stored in the sketch: Arbeitsprobe_Code.ino
#include <LiquidCrystal.h> //LCD library
LiquidCrystal lcd(13,12,11,10,9,8); //sets up pins connected to LCD display

#include <elapsedMillis.h> //library introduces elapsedmillis varibale
elapsedMillis tim; // variable stores amount of time elapsed in milliseconds
#define interval 5000//defined length of time sensor is calibrated in milliseconds

const int sensorPin = A0; //const value stores sensor pin being used to check analog readings from tempertaure sensor
float baselineTemp = 20.0; // every 2 degrees above this baseline temp, turns on the next LED, default baseline temperature is set to 20 degrees celsius
float temperature= 0.0; //stores value of the temperature when voltage is converted
int sensorVal = 0; // stores the value read by the temperature sensor
int switchState = 0; //switch used to calibrate room temperature.
int sensorMin = 1023; // minimum sensor value reading set first to 1023
int sensorMax = 0; // maximum sensor value reading set first to 0
int switchpin = 5; //stores value at which input is the switch pin read
int LEDCalibrate = 6; // stores value at which output LED pin used for calibration is at
void setup() {
  Serial.begin(9600); //open a serial port connection between Arduino and computer, so analog values that are input appear on serial monitor. 
                     //9600 represents bits per second transfer rate.
  for(int pinNumber = 2; pinNumber<5; pinNumber++){ //for loop simplifies declaration of pinMode running through pins 2 to 4.
      pinMode(pinNumber,OUTPUT);
      digitalWrite(pinNumber,LOW);
    }
   
    
     pinMode(switchpin,INPUT);   //reads switch used to turn on LED to signal the start of the calibration period.
    pinMode(LEDCalibrate, OUTPUT);
    digitalWrite(LEDCalibrate, LOW);
    tim=0;
    lcd.begin(16,2); //sets up number of rows and columns on LCD
}

void loop() {
 switchState = digitalRead(switchpin);
 if(switchState == LOW){ //as long as switch is not pressed baseline temperature is not changed and program continues to read temperature
  int sensorVal = analogRead(sensorPin); //Analog read will be an integer between 0 and 1023. 
  Serial.print("\nSensor Value: "); 
  Serial.print(sensorVal);
  
  float voltage = (sensorVal/1024.0) * 5.0; //converts analog reading reading to volatage. Analog reading goes up to 1024 and voltage goes up to 5V.
  Serial.print(", Volts: ");
  Serial.print(voltage);
  
  Serial.print(", Degrees C: ");
  float temperature = (voltage - .5) * 100; // datasheet provided for the sensor indicates what temperature is being read based on the voltage. 
                                           //In this case every 10 millivolts of change represents 1 degree Celsius of temp change
  Serial.print(temperature);

  if(temperature < baselineTemp + 1){
          digitalWrite(2,LOW);
          digitalWrite(3,LOW);
          digitalWrite(4,LOW);
    }
    else if (temperature >= baselineTemp+2 && temperature < baselineTemp+4){
          digitalWrite(2,HIGH);
          digitalWrite(3,LOW);
          digitalWrite(4,LOW);
    }else if (temperature >= baselineTemp+4 && temperature < baselineTemp+6){
          digitalWrite(2,HIGH);
          digitalWrite(3,HIGH);
          digitalWrite(4,LOW);
    }else if (temperature >= baselineTemp+6){
          digitalWrite(2,HIGH);
          digitalWrite(3,HIGH);
          digitalWrite(4,HIGH);
    }
        lcd.setCursor(0,1);
        lcd.print("Temp Deg C: ");
        lcd.print(temperature);
        delay(1000); //Analog readings can only be done so fast hence delay.
   }
  else//if(switchState == HIGH)
   { //once switch is pressed temperature is read and baseline temperature is recalibrated. Takes 5 seconds
      tim=0;//set timer to go back to zero
       while (tim < interval) { //as long as time elapsed is less than 5 seconds
     digitalWrite(LEDCalibrate,HIGH); // LED at pin 9 is turned on during calibration
     sensorVal= analogRead(sensorPin);
     // record the maximum sensor value
    if (sensorVal > sensorMax) {
      sensorMax = sensorVal;
    }

    // record the minimum sensor value
    if (sensorVal < sensorMin) {
      sensorMin = sensorVal;
    }
  }
        sensorVal = (sensorMax + sensorMin)/2; //determines the average sensor reading within the 5 second time frame 
        float voltage = (sensorVal/1024.0) * 5.0; 
  
        
        float temperature = (voltage - .5) * 100; 
       
        baselineTemp = temperature;
        Serial.print("\n New base temperature: ");
        Serial.print(baselineTemp);  
        lcd.setCursor(0,1);
        lcd.write("base Temp: ");
        lcd.write(baselineTemp);
        delay(5000);
        digitalWrite(LEDCalibrate,LOW); // LED at pin 9 is turned off once calibration is finished
}
}
